// Logisim project control_logic.circ as structural Verilog: 1 circuit, main circuit control_logic
module control_logic (
  input  [31:0] inst,
  input  BrEq,
  input  BrLt,
  output PCSel,
  output RegWEn,
  output [2:0] ImmSel,
  output BrUn,
  output ASel,
  output BSel,
  output [3:0] ALUSel,
  output MemRW,
  output [1:0] WBSel,
  output CSRSel,
  output CSRWen
);

  wire and_1_out, and_2_out, and_3_out, and_4_out, and_5_out, and_6_out, and_7_out, comparator_6_eq,
       comparator_7_eq, comparator_10_eq, comparator_11_eq, comparator_12_eq, comparator_13_eq,
       comparator_14_eq, comparator_15_eq, comparator_16_eq, comparator_17_eq, comparator_18_eq,
       comparator_19_eq, comparator_20_eq, comparator_21_eq, comparator_22_eq, comparator_23_eq,
       comparator_24_eq, comparator_25_eq, comparator_26_eq, comparator_27_eq, comparator_28_eq,
       comparator_29_eq, comparator_30_eq, comparator_31_eq, comparator_32_eq, comparator_33_eq,
       comparator_34_eq, comparator_35_eq, comparator_36_eq, comparator_37_eq, comparator_38_eq,
       comparator_39_eq, IJtype, ILtype, isadd, isand, isbeq, isbge, isbgeu, isblt, isbltu, isbne, ismul,
       ismulh, ismulhu, isor, issll, isslt, issra, issrl, issub, isxor, Itype, not_1_out, not_2_out,
       not_3_out, or_2_out, or_4_out, or_5_out, or_7_out, Rtype, SBtype, Stype, UJtype, Utype;
  wire [2:0] multiplexer_5_out, multiplexer_6_out, multiplexer_10_out;
  wire [3:0] multiplexer_1_out, multiplexer_2_out, multiplexer_3_out, multiplexer_4_out, multiplexer_8_out,
       multiplexer_9_out, multiplexer_11_out, multiplexer_12_out, multiplexer_15_out, multiplexer_17_out;

  Multiplexer #(.width(4)) multiplexer_1 (.in0(4'b0000), .in1(4'b0001), .out(multiplexer_1_out), .sel(isand));
  Multiplexer #(.width(4)) multiplexer_2 (.in0(multiplexer_1_out), .in1(4'b0010), .out(multiplexer_2_out), .sel(isor));
  Multiplexer #(.width(4)) multiplexer_3 (
    .in0(multiplexer_17_out), .in1(4'b1010), .out(multiplexer_3_out), .sel(ismul));
  Multiplexer #(.width(4)) multiplexer_4 (
    .in0(multiplexer_3_out), .in1(4'b1011), .out(multiplexer_4_out), .sel(ismulhu));
  Multiplexer #(.width(3)) multiplexer_5 (.in0(3'b000), .in1(3'b001), .out(multiplexer_5_out), .sel(Stype));
  Multiplexer #(.width(3)) multiplexer_6 (.in0(multiplexer_5_out), .in1(3'b010), .out(multiplexer_6_out), .sel(SBtype));
  Multiplexer multiplexer_7 (.in0(1'b0), .in1(1'b1), .out(BSel), .sel(or_2_out));
  or or_1 (BrUn, isbgeu, isbltu);
  and and_1 (and_1_out, BrEq, isbeq);
  not not_1 (not_1_out, BrEq);
  and and_2 (and_2_out, not_1_out, isbne);
  and and_3 (and_3_out, BrLt, isblt);
  not not_2 (not_2_out, BrLt);
  and and_4 (and_4_out, not_2_out, isbge);
  and and_5 (and_5_out, BrLt, isbltu);
  not not_3 (not_3_out, BrLt);
  and and_6 (and_6_out, not_3_out, isbgeu);
  Multiplexer #(.width(4)) multiplexer_8 (.in0(multiplexer_2_out), .in1(4'b0011), .out(multiplexer_8_out), .sel(isxor));
  Multiplexer #(.width(4)) multiplexer_9 (.in0(multiplexer_4_out), .in1(4'b1100), .out(multiplexer_9_out), .sel(issub));
  Multiplexer #(.width(3)) multiplexer_10 (
    .in0(multiplexer_6_out), .in1(3'b011), .out(multiplexer_10_out), .sel(Utype));
  or or_2 (or_2_out, ILtype, Itype, Utype, IJtype, SBtype, UJtype);
  Multiplexer #(.width(4)) multiplexer_11 (
    .in0(multiplexer_8_out), .in1(4'b0100), .out(multiplexer_11_out), .sel(issrl));
  Multiplexer #(.width(4)) multiplexer_12 (
    .in0(multiplexer_11_out), .in1(4'b0101), .out(multiplexer_12_out), .sel(issra));
  Multiplexer #(.width(4)) multiplexer_13 (.in0(multiplexer_9_out), .in1(4'b1110), .out(ALUSel), .sel(ismulh));
  Multiplexer #(.width(3)) multiplexer_14 (.in0(multiplexer_10_out), .in1(3'b100), .out(ImmSel), .sel(UJtype));
  or or_3 (RegWEn, Rtype, Itype, ILtype, Utype, UJtype, IJtype);
  and and_7 (and_7_out, SBtype, or_4_out);
  or or_4 (or_4_out, and_1_out, and_2_out, and_3_out, and_4_out, and_5_out, and_6_out);
  Multiplexer #(.width(4)) multiplexer_15 (
    .in0(multiplexer_12_out), .in1(4'b0110), .out(multiplexer_15_out), .sel(issll));
  Multiplexer #(.width(2)) multiplexer_16 (.in0(2'b01), .in1(2'b10), .out(WBSel), .sel(or_5_out));
  or or_5 (or_5_out, IJtype, UJtype);
  or or_6 (PCSel, UJtype, IJtype, and_7_out);
  Comparator #(.width(7)) comparator_1 (.a(inst[6:0]), .b(7'b0110011), .eq(Rtype));  // open: gt, lt
  Comparator #(.width(7)) comparator_2 (.a(inst[6:0]), .b(7'b0000011), .eq(ILtype));  // open: gt, lt
  Comparator #(.width(7)) comparator_3 (.a(inst[6:0]), .b(7'b0010011), .eq(Itype));  // open: gt, lt
  Comparator #(.width(7)) comparator_4 (.a(inst[6:0]), .b(7'b0100011), .eq(Stype));  // open: gt, lt
  Comparator #(.width(7)) comparator_5 (.a(inst[6:0]), .b(7'b1100011), .eq(SBtype));  // open: gt, lt
  Comparator #(.width(7)) comparator_6 (.a(inst[6:0]), .b(7'b0010111), .eq(comparator_6_eq));  // open: gt, lt
  Comparator #(.width(7)) comparator_7 (.a(inst[6:0]), .b(7'b0110111), .eq(comparator_7_eq));  // open: gt, lt
  Comparator #(.width(7)) comparator_8 (.a(inst[6:0]), .b(7'b1101111), .eq(UJtype));  // open: gt, lt
  Comparator #(.width(7)) comparator_9 (.a(inst[6:0]), .b(7'b1100111), .eq(IJtype));  // open: gt, lt
  Multiplexer #(.width(4)) multiplexer_17 (
    .in0(multiplexer_15_out), .in1(4'b0111), .out(multiplexer_17_out), .sel(isslt));
  Multiplexer multiplexer_18 (.in0(1'b0), .in1(1'b1), .out(ASel), .sel(or_7_out));
  or or_7 (or_7_out, SBtype, UJtype);
  or or_8 (Utype, comparator_6_eq, comparator_7_eq);
  Comparator #(.mode("unsigned"), .width(3)) comparator_10 (
    .a(inst[14:12]), .b(3'b000), .eq(comparator_10_eq));  // open: gt, lt
  Comparator #(.mode("unsigned"), .width(7)) comparator_11 (
    .a(inst[31:25]), .b({7{1'b0}}), .eq(comparator_11_eq));  // open: gt, lt
  Comparator #(.mode("unsigned"), .width(3)) comparator_12 (
    .a(inst[14:12]), .b(3'b000), .eq(comparator_12_eq));  // open: gt, lt
  Comparator #(.mode("unsigned"), .width(7)) comparator_13 (
    .a(inst[31:25]), .b(7'b0100000), .eq(comparator_13_eq));  // open: gt, lt
  Comparator #(.mode("unsigned"), .width(3)) comparator_14 (
    .a(inst[14:12]), .b(3'b000), .eq(comparator_14_eq));  // open: gt, lt
  Comparator #(.mode("unsigned"), .width(7)) comparator_15 (
    .a(inst[31:25]), .b(7'b0000001), .eq(comparator_15_eq));  // open: gt, lt
  Comparator #(.mode("unsigned"), .width(3)) comparator_16 (
    .a(inst[14:12]), .b(3'b001), .eq(comparator_16_eq));  // open: gt, lt
  Comparator #(.mode("unsigned"), .width(7)) comparator_17 (
    .a(inst[31:25]), .b({7{1'b0}}), .eq(comparator_17_eq));  // open: gt, lt
  Comparator #(.mode("unsigned"), .width(3)) comparator_18 (
    .a(inst[14:12]), .b(3'b001), .eq(comparator_18_eq));  // open: gt, lt
  Comparator #(.mode("unsigned"), .width(7)) comparator_19 (
    .a(inst[31:25]), .b(7'b0000001), .eq(comparator_19_eq));  // open: gt, lt
  Comparator #(.mode("unsigned"), .width(3)) comparator_20 (
    .a(inst[14:12]), .b(3'b010), .eq(comparator_20_eq));  // open: gt, lt
  Comparator #(.mode("unsigned"), .width(7)) comparator_21 (
    .a(inst[31:25]), .b({7{1'b0}}), .eq(comparator_21_eq));  // open: gt, lt
  Comparator #(.mode("unsigned"), .width(3)) comparator_22 (
    .a(inst[14:12]), .b(3'b011), .eq(comparator_22_eq));  // open: gt, lt
  Comparator #(.mode("unsigned"), .width(7)) comparator_23 (
    .a(inst[31:25]), .b(7'b0000001), .eq(comparator_23_eq));  // open: gt, lt
  Comparator #(.mode("unsigned"), .width(3)) comparator_24 (
    .a(inst[14:12]), .b(3'b100), .eq(comparator_24_eq));  // open: gt, lt
  Comparator #(.mode("unsigned"), .width(7)) comparator_25 (
    .a(inst[31:25]), .b({7{1'b0}}), .eq(comparator_25_eq));  // open: gt, lt
  Comparator #(.mode("unsigned"), .width(3)) comparator_26 (
    .a(inst[14:12]), .b(3'b101), .eq(comparator_26_eq));  // open: gt, lt
  Comparator #(.mode("unsigned"), .width(7)) comparator_27 (
    .a(inst[31:25]), .b({7{1'b0}}), .eq(comparator_27_eq));  // open: gt, lt
  Comparator #(.mode("unsigned"), .width(3)) comparator_28 (
    .a(inst[14:12]), .b(3'b101), .eq(comparator_28_eq));  // open: gt, lt
  Comparator #(.mode("unsigned"), .width(7)) comparator_29 (
    .a(inst[31:25]), .b(7'b0100000), .eq(comparator_29_eq));  // open: gt, lt
  Comparator #(.mode("unsigned"), .width(3)) comparator_30 (
    .a(inst[14:12]), .b(3'b110), .eq(comparator_30_eq));  // open: gt, lt
  Comparator #(.mode("unsigned"), .width(7)) comparator_31 (
    .a(inst[31:25]), .b({7{1'b0}}), .eq(comparator_31_eq));  // open: gt, lt
  Comparator #(.mode("unsigned"), .width(3)) comparator_32 (
    .a(inst[14:12]), .b(3'b111), .eq(comparator_32_eq));  // open: gt, lt
  Comparator #(.mode("unsigned"), .width(7)) comparator_33 (
    .a(inst[31:25]), .b({7{1'b0}}), .eq(comparator_33_eq));  // open: gt, lt
  and and_8 (isadd, Rtype, comparator_10_eq, comparator_11_eq);
  and and_9 (issub, Rtype, comparator_12_eq, comparator_13_eq);
  and and_10 (ismul, Rtype, comparator_14_eq, comparator_15_eq);
  and and_11 (issll, Rtype, comparator_16_eq, comparator_17_eq);
  and and_12 (ismulh, Rtype, comparator_18_eq, comparator_19_eq);
  and and_13 (isslt, Rtype, comparator_20_eq, comparator_21_eq);
  and and_14 (ismulhu, Rtype, comparator_22_eq, comparator_23_eq);
  and and_15 (isxor, Rtype, comparator_24_eq, comparator_25_eq);
  and and_16 (issrl, Rtype, comparator_26_eq, comparator_27_eq);
  and and_17 (issra, Rtype, comparator_28_eq, comparator_29_eq);
  and and_18 (isor, Rtype, comparator_30_eq, comparator_31_eq);
  and and_19 (isand, Rtype, comparator_32_eq, comparator_33_eq);
  Comparator #(.mode("unsigned"), .width(3)) comparator_34 (
    .a(inst[14:12]), .b(3'b000), .eq(comparator_34_eq));  // open: gt, lt
  Comparator #(.mode("unsigned"), .width(3)) comparator_35 (
    .a(inst[14:12]), .b(3'b001), .eq(comparator_35_eq));  // open: gt, lt
  Comparator #(.mode("unsigned"), .width(3)) comparator_36 (
    .a(inst[14:12]), .b(3'b100), .eq(comparator_36_eq));  // open: gt, lt
  Comparator #(.mode("unsigned"), .width(3)) comparator_37 (
    .a(inst[14:12]), .b(3'b101), .eq(comparator_37_eq));  // open: gt, lt
  Comparator #(.mode("unsigned"), .width(3)) comparator_38 (
    .a(inst[14:12]), .b(3'b110), .eq(comparator_38_eq));  // open: gt, lt
  Comparator #(.mode("unsigned"), .width(3)) comparator_39 (
    .a(inst[14:12]), .b(3'b111), .eq(comparator_39_eq));  // open: gt, lt
  and and_20 (isbeq, SBtype, comparator_34_eq);
  and and_21 (isbne, SBtype, comparator_35_eq);
  and and_22 (isblt, SBtype, comparator_36_eq);
  and and_23 (isbge, SBtype, comparator_37_eq);
  and and_24 (isbltu, SBtype, comparator_38_eq);
  and and_25 (isbgeu, SBtype, comparator_39_eq);

  assign CSRSel = 1'b0;
  assign CSRWen = 1'b0;
  assign MemRW = 1'b0;

  // Other names for the same wires on the sheet: opcode[6:0] = inst[6:0]; rd[4:0] = inst[11:7];
  //   funct3[2:0] = inst[14:12]; rs1[4:0] = inst[19:15]; rs2[4:0] = inst[24:20]; funct7[6:0] = inst[31:25]

  // Notes on the sheet:
  //   INPUTS to your circuit
  //   DON'T CHANGE THE LOCATIONS OF THE INPUTS AND OUTPUTS!
  //   OUTPUT from your circuit
endmodule
